// Logisim project SAP-2.circ as structural Verilog
module CPU (
  input  in_1,
  input  HLT,
  input  CLR,
  input  [6:0] in_4,
  output [6:0] out_5,
  output [7:0] out_6,
  output Negative,
  output Zero,
  output Not_Zero,
  output [7:0] out_10,
  output [7:0] out_11,
  output Serial_Out,
  output lol
);

  wire ACKNOWLEDGE, AND, Au, CE, CLeR, CLK, CLK_2_out, CLK_out, CLKr, Cm, CMA, controlled_buffer_1_out, Cp,
       DCR, DON, Du, Ea, Eb, Ec, Ei, Ein1, Ein2, Ep, Etm, FN, FZ, HLT_t, INR, JM, JNZ, JZ, La, Lb, Lc, Lf,
       Li, Lm, Lmd, Lo3, Lo4, Lp, Ltm, Mu, not_1_out, OR, or_1_out, or_3_out, RAL, RAR, READY, RET, Su, XOR;
  wire [7:0] A_out_9, IR_out_6, IR_out_7, MDR_out_6, PC_out_9, TMP_out_7;
  wire [15:0] MAR_out_7;

  Button u_CLK (.out(CLK_out));
  Clock CLK_2 (.out(CLK_2_out));
  assign controlled_buffer_1_out = or_1_out ? CLK_2_out : 1'bz;  // Controlled_Buffer controlled_buffer_1
  or or_1 (or_1_out, HLT, not_1_out);
  not not_1 (not_1_out, HLT_t);
  or or_2 (CLK, CLK_out, controlled_buffer_1_out);
  IR IR (.minus_Li(Li), .minus_Ei(Ei), .CLK(CLK), .CLR(CLR), .out_6(IR_out_6), .out_7(IR_out_7), .in_1(IR_out_6));
  PC PC (
    .out_8(IR_out_6), .Lp(Lp), .Ep(Ep), .out_9(PC_out_9), .Cp(Cp), .CLK(CLK), .CLR(CLR), .in_6(IR_out_6),
    .in_7(DON));
  MAR MAR (.Lma(Lm), .CLK(CLK), .in_1(IR_out_6), .in_4(PC_out_9), .out_7(MAR_out_7), .Cm(Cm), .RET(RET));
  MDR MDR (.Lmd(Lmd), .CLK(CLK), .out_6(MDR_out_6), .in_3(IR_out_6), .in_4(PC_out_9), .DON(DON));
  Keyboard keyboard_1 (.clk(CLK), .re(ACKNOWLEDGE), .clr(in_1), .avail(READY), .data(out_5));
  // Probe on IR_out_6
  // Probe on IR_out_6
  // Probe on IR_out_6
  RAM_part #(.addrWidth(16), .bus("separate")) ram_1 (
    .addr(MAR_out_7), .din(MDR_out_6), .data(IR_out_6), .clk(CLKr), .ld(CE));  // open: str, sel, clr
  // Probe on IR_out_6
  // Probe on IR_out_7
  or or_3 (or_3_out, DON, CLR);
  In_port_1 u_IN_1 (.Ei1(Ein1), .in_2(out_5), .CLK(CLK), .out_4(IR_out_6));
  In_port_2 IN_2 (.READY(READY), .in_2(in_4), .Ei2(Ein2), .CLK(CLK), .out_5(IR_out_6));
  // Probe on PC_out_9
  // Probe on IR_out_6
  Controller CONTROLLER (
    .in_1(IR_out_7[7]), .in_2(IR_out_7[6]), .OPcode(IR_out_7[5]), .in_4(IR_out_7[4]), .in_5(IR_out_7[3]),
    .in_6(IR_out_7[2]), .in_7(IR_out_7[1]), .in_8(IR_out_7[0]), .in_9(CLK), .Lf(Lf), .FN(FN), .FZ(FZ),
    .FC(1'b0), .DON(or_3_out), .out_18(Lp), .out_19(Ep), .Lp(Cp), .Ep(Lm), .Cp(Cm), .Lm(Lmd), .Lmd(CE),
    .CE(CLKr), .CLKr(Li), .Li(Ei), .Ei(INR), .INR(DCR), .DCR(RAR), .RAR(RAL), .RAL(JNZ), .JNZ(JZ), .JZ_2(JM),
    .JM_2(CMA), .CMA(XOR), .XOR(OR), .OR(AND), .AND(Du), .Du(Mu), .Mu(Su), .Su(Au), .Au(La), .La(Ea),
    .Ea(Ltm), .Ltm(Etm), .Etm(Lb), .Lb(Eb), .Eb(Lc), .Lc(Ec), .Ec(Ein1), .Ein1(Ein2), .Ein2(Lo3), .Lo3(Lo4),
    .Lo4(CLeR), .CLK(HLT_t), .CLR(DON), .HLT(Lf), .DON_2(RET), .JM(JM), .JZ(JZ), .JC(1'b0));
  Out_port_3 OUT_3 (.CLK(Lo3), .in_3(CLK), .out_5(out_11), .minus_Lo(IR_out_6), .CLR(CLR));
  // Probe on IR_out_6
  ALU ALU (
    .in_1(A_out_9), .in_2(TMP_out_7), .DIV(Du), .MUL(Mu), .SUB(Su), .ADD(Au), .out_16(IR_out_6), .AND(AND),
    .OR(OR), .CMA(CMA), .XOR(XOR), .RAL(RAL), .RAR(RAR), .Negative_2(Negative), .Zero(Zero),
    .NotZero(Not_Zero), .DCR(DCR), .INR(INR));  // open: Overflow, Negative
  Out_port_4 OUT_4 (
    .in_1(IR_out_6), .Lo4(Lo4), .CLK(CLK), .ACKNOWLEDGE(ACKNOWLEDGE), .Serial_Out(Serial_Out), .CLR(CLR));
  Accumulator_A A (
    .Negative(FN), .Zero(FZ), .minus_La(La), .in_2(IR_out_6), .CLK(CLK), .CLR(CLR), .Ea(Ea), .out_9(A_out_9),
    .out_10(IR_out_6), .out_8(out_6));
  TMP TMP (
    .Ltm(Ltm), .CLK(CLK), .CLR(CLR), .Etm(Etm), .out_7(TMP_out_7), .out_8(IR_out_6), .in_2(IR_out_6),
    .out_6(out_10));
  B_Reg B (.Lb(Lb), .in_2(IR_out_6), .CLK(CLK), .CLR(CLR), .Eb(Eb), .out_6(IR_out_6));
  C_Reg C (.Lb(Lc), .in_2(IR_out_6), .CLK(CLK), .CLR(CLR), .Eb(Ec), .out_6(IR_out_6));

  // Notes on the sheet:
  //   RAM
  //   Hexadecimal Keyboard
  //   W Bus
  //   JC
  //   FC
endmodule

module In_port_1 (
  input  Ei1,
  input  [6:0] in_2,
  input  CLK,
  output [7:0] out_4
);

  wire not_1_out;
  wire [7:0] bit_extender_1_out, register_1_q;

  assign bit_extender_1_out = {{1{1'b0}}, in_2};  // Bit_Extender bit_extender_1
  not not_1 (not_1_out, CLK);
  Register register_1 (.D(bit_extender_1_out), .Q(register_1_q), .clk(not_1_out));  // open: en, clr
  assign out_4 = Ei1 ? register_1_q : 8'bz;  // Controlled_Buffer controlled_buffer_1
endmodule

module In_port_2 (
  input  READY,
  input  [6:0] in_2,
  input  CLK,
  input  Ei2,
  output [7:0] out_5
);

  wire not_1_out;
  wire [7:0] register_1_q;

  Register register_1 (.D({in_2, READY}), .Q(register_1_q), .clk(not_1_out));  // open: en, clr
  not not_1 (not_1_out, CLK);
  assign out_5 = Ei2 ? register_1_q : 8'bz;  // Controlled_Buffer controlled_buffer_1
endmodule

module PC (
  input  Lp,
  input  Ep,
  input  Cp,
  input  CLK,
  input  CLR,
  input  [7:0] in_6,
  input  in_7,
  output [7:0] out_8,
  output [7:0] out_9
);

  wire d_ff_1_qn, d_ff_2_qn, not_1_out, or_1_out, t_ff_1_q;
  wire [7:0] demultiplexer_1_out0, demultiplexer_1_out1;
  wire [15:0] counter_1_q, register_1_q;

  D_Flip_Flop #(.trigger("high")) d_ff_1 (.clk(CLK), .D(1'b1), .Qn(d_ff_1_qn));  // open: Q, preset, en, reset
  D_Flip_Flop d_ff_2 (.clk(CLK), .D(1'b1), .Qn(d_ff_2_qn), .preset(or_1_out), .reset(Lp));  // open: Q, en
  or or_1 (or_1_out, d_ff_1_qn, Cp);
  not not_1 (not_1_out, CLK);
  Counter #(.width(16), .max('hffff)) counter_1 (
    .load(d_ff_2_qn), .D(register_1_q), .count(Cp), .Q(counter_1_q), .clk(not_1_out), .clr(CLR));  // open: carry
  assign {out_9, out_8} = Ep ? counter_1_q : 16'bz;  // Controlled_Buffer controlled_buffer_1
  Register #(.trigger("high")) register_1 (
    .D(demultiplexer_1_out0), .Q(register_1_q[7:0]), .clk(CLK));  // open: en, clr
  Register #(.trigger("high")) register_2 (
    .D(demultiplexer_1_out1), .Q(register_1_q[15:8]), .clk(CLK));  // open: en, clr
  // Probe on demultiplexer_1_out1
  // Probe on demultiplexer_1_out0
  T_Flip_Flop #(.trigger("falling")) t_ff_1 (
    .clk(d_ff_2_qn), .T(1'b1), .Q(t_ff_1_q), .reset(in_7));  // open: Qn, preset, en
  Demultiplexer #(.width(8), .tristate("true"), .enable("false")) demultiplexer_1 (
    .out0(demultiplexer_1_out0), .out1(demultiplexer_1_out1), .in(in_6), .sel(t_ff_1_q));
endmodule

module MAR (
  input  [7:0] in_1,
  input  Lma,
  input  RET,
  input  [7:0] in_4,
  input  Cm,
  input  CLK,
  output [15:0] out_7
);

  wire not_1_out, or_1_out;
  wire [15:0] controlled_buffer_1_out;

  assign controlled_buffer_1_out = RET ? 16'hfffe : 16'bz;  // Controlled_Buffer controlled_buffer_1
  or or_1 (or_1_out, RET, Lma);
  assign controlled_buffer_1_out = Lma ? {in_4, in_1} : 16'bz;  // Controlled_Buffer controlled_buffer_2
  Counter #(.width(16), .max('hffff)) counter_1 (
    .load(or_1_out), .D(controlled_buffer_1_out), .count(Cm), .Q(out_7), .clk(not_1_out));  // open: carry, clr
  not not_1 (not_1_out, CLK);

  // Notes on the sheet:
  //   W bus
endmodule

module RAM (
  input  [7:0] in_1,
  input  [7:0] in_2,
  input  in_3,
  input  in_4,
  output [7:0] out_5
);

  wire clock_1_out;

  Clock clock_1 (.out(clock_1_out));
  RAM_part #(.bus("separate")) ram_1 (
    .addr(in_1), .din(in_2), .data(out_5), .str(in_3), .clk(clock_1_out), .ld(in_4));  // open: sel, clr
endmodule

module MDR (
  input  Lmd,
  input  CLK,
  input  [7:0] in_3,
  input  [7:0] in_4,
  input  DON,
  output [7:0] out_6
);

  wire not_1_out, t_ff_1_qn;
  wire [7:0] multiplexer_1_out;

  Register register_1 (.D(multiplexer_1_out), .en(Lmd), .Q(out_6), .clk(not_1_out));  // open: clr
  not not_1 (not_1_out, CLK);
  Multiplexer #(.width(8), .enable("false")) multiplexer_1 (
    .in0(in_3), .in1(in_4), .out(multiplexer_1_out), .sel(t_ff_1_qn));
  T_Flip_Flop t_ff_1 (.clk(Lmd), .T(1'b1), .Qn(t_ff_1_qn), .reset(DON));  // open: Q, preset, en
endmodule

module IR (
  input  [7:0] in_1,
  input  minus_Li,
  input  minus_Ei,
  input  CLK,
  input  CLR,
  output [7:0] out_6,
  output [7:0] out_7
);

  wire not_1_out;

  Register register_1 (.D(in_1), .en(minus_Li), .Q(out_7), .clk(not_1_out), .clr(CLR));
  not not_1 (not_1_out, CLK);
  assign out_6 = minus_Ei ? out_7 : 8'bz;  // Controlled_Buffer controlled_buffer_1

  // Notes on the sheet:
  //   For W Bus
  //   For Controller
endmodule

module Controller (
  input  in_1,
  input  in_2,
  input  OPcode,
  input  in_4,
  input  in_5,
  input  in_6,
  input  in_7,
  input  in_8,
  input  in_9,
  input  Lf,
  input  JM,
  input  JZ,
  input  JC,
  input  FN,
  input  FZ,
  input  FC,
  input  DON,
  output out_18,
  output out_19,
  output Lp,
  output Ep,
  output Cp,
  output Lm,
  output Lmd,
  output CE,
  output CLKr,
  output Li,
  output Ei,
  output INR,
  output DCR,
  output RAR,
  output RAL,
  output JNZ,
  output JZ_2,
  output JM_2,
  output CMA,
  output XOR,
  output OR,
  output AND,
  output Du,
  output Mu,
  output Su,
  output Au,
  output La,
  output Ea,
  output Ltm,
  output Etm,
  output Lb,
  output Eb,
  output Lc,
  output Ec,
  output Ein1,
  output Ein2,
  output Lo3,
  output Lo4,
  output CLK,
  output CLR,
  output HLT,
  output DON_2
);

  wire and_1_out, and_2_out, and_3_out, controlled_buffer_1_out, controlled_buffer_2_out,
       controlled_buffer_3_out, decoder_1_out0, decoder_1_out1, decoder_1_out2, not_1_out, or_1_out;
  wire [7:0] counter_1_q;
  wire [20:0] rom_1_data, rom_2_data, rom_3_data;

  and and_1 (and_1_out, Lf, JM);
  and and_2 (and_2_out, Lf, JZ);
  and and_3 (and_3_out, Lf, JC);
  assign controlled_buffer_1_out = and_1_out ? FN : 1'bz;  // Controlled_Buffer controlled_buffer_1
  assign controlled_buffer_2_out = and_2_out ? FZ : 1'bz;  // Controlled_Buffer controlled_buffer_2
  assign controlled_buffer_3_out = and_3_out ? FC : 1'bz;  // Controlled_Buffer controlled_buffer_3
  D_Flip_Flop #(.trigger("high")) d_ff_1 (
    .clk(Lf), .Q(counter_1_q[5]), .preset(controlled_buffer_1_out), .reset(DON));  // open: D, Qn, en
  D_Flip_Flop #(.trigger("falling")) d_ff_2 (
    .clk(Lf), .Q(counter_1_q[6]), .preset(controlled_buffer_2_out), .reset(DON));  // open: D, Qn, en
  D_Flip_Flop #(.trigger("falling")) d_ff_3 (
    .clk(Lf), .Q(counter_1_q[7]), .preset(controlled_buffer_3_out), .reset(DON));  // open: D, Qn, en
  ROM #(.addrWidth(5), .dataWidth(21)) rom_1 (.addr(counter_1_q[4:0]), .data(rom_1_data));  // open: sel
  ROM #(.addrWidth(16), .dataWidth(21)) rom_2 (
    .addr({in_1, in_2, OPcode, in_4, in_5, in_6, in_7, in_8, counter_1_q}), .data(rom_2_data));  // open: sel
  ROM #(.addrWidth(16), .dataWidth(21)) rom_3 (
    .addr({in_1, in_2, OPcode, in_4, in_5, in_6, in_7, in_8, counter_1_q}), .data(rom_3_data));  // open: sel
  Decoder #(.select(5), .enable("false")) decoder_1 (
    .out0(decoder_1_out0), .out1(decoder_1_out1), .out2(decoder_1_out2), .sel(counter_1_q[4:0]));  // open: out3, out4, out5, out6, out7, out8, out9, out10, out11, out12, out13, out14, out15, out16, out17, out18, out19, out20, out21, out22, out23, out24, out25, out26, out27, out28, out29, out30, out31
  Counter #(.width(5), .max('h1f)) counter_1 (
    .Q(counter_1_q[4:0]), .clk(in_9), .clr(DON));  // open: load, D, count, carry
  or or_1 (or_1_out, decoder_1_out0, decoder_1_out1, decoder_1_out2);
  not not_1 (not_1_out, or_1_out);
  assign {out_18, out_19, Lp, Ep, Cp, Lm, Lmd, CE, CLKr, Li, Ei, INR, DCR, RAR, RAL, JNZ, JZ_2, JM_2, CMA, XOR, OR} = not_1_out ? rom_2_data : 21'bz;  // Controlled_Buffer controlled_buffer_4
  assign {AND, Du, Mu, Su, Au, La, Ea, Ltm, Etm, Lb, Eb, Lc, Ec, Ein1, Ein2, Lo3, Lo4, CLK, CLR, HLT, DON_2} = not_1_out ? rom_3_data : 21'bz;  // Controlled_Buffer controlled_buffer_5
  assign {out_18, out_19, Lp, Ep, Cp, Lm, Lmd, CE, CLKr, Li, Ei, INR, DCR, RAR, RAL, JNZ, JZ_2, JM_2, CMA, XOR, OR} = or_1_out ? rom_1_data : 21'bz;  // Controlled_Buffer controlled_buffer_6
  Pull_Resistor pull_resistor_1 (.node({out_18, out_19, Lp, Ep, Cp, Lm, Lmd, CE, CLKr, Li, Ei, INR, DCR, RAR, RAL, JNZ, JZ_2, JM_2, CMA, XOR, OR}));
  Pull_Resistor pull_resistor_2 (.node({AND, Du, Mu, Su, Au, La, Ea, Ltm, Etm, Lb, Eb, Lc, Ec, Ein1, Ein2, Lo3, Lo4, CLK, CLR, HLT, DON_2}));

  // Notes on the sheet:
  //   ROM 0
  //   ROM A
  //   ROM B
  //   contents of rom_1 (hex, n*v repeats v):
  //   a0000 40000 5000
  //   contents of rom_2 (hex, n*v repeats v):
  //   5123*0 400 256*0 400 255*0 400 510*0 200 256*0 200 255*0 200 11007*0 1 255*0 1 767*0 2 255*0 2 767*0
  //   4 255*0 4 510*0 a0000 4000 40001 253*0 a0000 4000 40002 253*0 a0000 4000 40004 1533*0 10000 104000
  //   10000 104000 252*0 40010 40000 31*0 10000 104000 10000 104000 219*0 40020 40000 63*0 10000 104000
  //   10000 104000 187*0 40020 10000 104000 10000 104000 59*0 40000 40000 3262*0 100 255*0 80 1791*0 8
  //   5119*0 88000 2000 98000 2000 a0000 104000 10000 104000 a0000 4000 0 104000 10000 104000 40000 40000
  //   240*0 88000 2000 98000 2000 a0000 104000 10000 104000 a0000 8000 2000 0 104000 10000 104000 40000
  //   40000 1775*0 88000 2000 98000 2000 a0000 104000 10000 104000 7160*0 10000 44000 254*0 10000 44000
  //   254*0 10000 44000 8447*0 104000 10000 104000 40000 40000
  //   contents of rom_3 (hex, n*v repeats v):
  //   1283*0 4800 30000 4 253*0 4200 30000 4 765*0 4800 50000 4 253*0 4200 50000 4 765*0 4800 90000 4
  //   253*0 4200 90000 4 765*0 4800 110000 4 253*0 4200 110000 4 509*0 10000 4 254*0 10800 1000 4 253*0
  //   10200 400 4 509*0 10000 4 254*0 10800 1000 4 253*0 10200 400 4 11005*0 4800 10000 4 253*0 4200 10000
  //   4 765*0 4800 10000 4 253*0 4200 10000 4 765*0 4800 10000 4 253*0 4200 10000 4 510*0 4000 10000 4
  //   253*0 4000 10000 4 253*0 4000 10000 4 1536*0 4 251*0 2 0 4 34*0 4 218*0 2 0 4 66*0 4 186*0 2 4*0 4
  //   60*0 4 3261*0 10000 4 254*0 10000 4 1790*0 10000 4 5118*0 1 8*0 10000 1 5*0 4 239*0 1 8*0 8000 0 1
  //   5*0 4 1774*0 1 7*0 4 1015*0 10800 4 1022*0 10200 4 1022*0 9000 4 1022*0 1200 4 1022*0 8400 4 1022*0
  //   c00 4 1023*0 10000 4 254*0 1000 4 254*0 400 4 509*0 10100 4 254*0 10080 4 254*0 8040 4 254*0 8020 4
  //   7166*0 1 5*0 4 4089*0 4 9215*0 8
endmodule

module Accumulator_A (
  input  minus_La,
  input  [7:0] in_2,
  input  CLK,
  input  CLR,
  input  Ea,
  output Negative,
  output Zero,
  output [7:0] out_8,
  output [7:0] out_9,
  output [7:0] out_10
);

  wire not_1_out;

  Register register_1 (.D(in_2), .en(minus_La), .Q({Negative, out_8[6:0]}), .clk(not_1_out), .clr(CLR));
  not not_1 (not_1_out, CLK);
  assign out_10 = Ea ? {Negative, out_8[6:0]} : 8'bz;  // Controlled_Buffer controlled_buffer_1
  nor nor_1 (Zero, out_8[0], out_8[1], out_8[2], out_8[3], out_8[4], out_8[5], out_8[6], Negative);

  assign out_8[7] = Negative;
  assign out_9 = {Negative, out_8[6:0]};

  // Notes on the sheet:
  //   For ALU
endmodule

module ALU (
  input  [7:0] in_1,
  input  [7:0] in_2,
  input  INR,
  input  DCR,
  input  RAR,
  input  RAL,
  input  CMA,
  input  XOR,
  input  OR,
  input  AND,
  input  DIV,
  input  MUL,
  input  SUB,
  input  ADD,
  output Overflow,
  output [7:0] out_16,
  output Negative,
  output Negative_2,
  output Zero,
  output NotZero
);

  wire adder_1_cout, and_2_out, and_3_out, decoder_1_out1, decoder_1_out2, decoder_1_out3, nor_2_out,
       or_3_out, or_6_out, SUB_2_out_4;
  wire [1:0] or_4_out;
  wire [3:0] priority_encoder_1_p1;
  wire [7:0] adder_1_out, adder_2_out, and_1_out, divider_1_out, divider_1_rem, multiplexer_1_out,
       multiplier_1_cout, multiplier_1_out, not_1_out, or_1_out, shifter_1_out, shifter_2_out, SUB_2_out_3,
       SUB_out_3, undriven, undriven_2, undriven_3, xor_1_out;

  Decoder #(.select(2), .enable("false")) decoder_1 (
    .out1(decoder_1_out1), .out2(decoder_1_out2), .out3(decoder_1_out3), .sel(or_4_out));  // open: out0
  Adder adder_1 (.a(in_1), .b(in_2), .out(adder_1_out), .cout(adder_1_cout));  // open: cin
  Multiplier multiplier_1 (.a(in_1), .b(in_2), .out(multiplier_1_out), .cout(multiplier_1_cout));  // open: cin
  Divider divider_1 (.a(in_1), .b(in_2), .out(divider_1_out), .rem(divider_1_rem));  // open: upper
  assign and_1_out = in_1 & in_2;  // AND_Gate and_1, 8 bits wide
  assign or_1_out = in_1 | in_2;  // OR_Gate or_1, 8 bits wide
  assign xor_1_out = in_1 ^ in_2;  // XOR_Gate xor_1, 8 bits wide
  assign not_1_out = ~in_1;  // NOT_Gate not_1, 8 bits wide
  SUB_2_s u_SUB (.in_1(in_1), .in_2(8'h1), .out_3(SUB_out_3));  // open: out_4
  and and_2 (and_2_out, decoder_1_out3, or_3_out);
  SUB_2_s SUB_2 (.in_1(in_1), .in_2(in_2), .out_3(SUB_2_out_3), .out_4(SUB_2_out_4));
  Shifter #(.shift("rl")) shifter_1 (.in(in_1), .\dist (3'b001), .out(shifter_1_out));
  Shifter #(.shift("rr")) shifter_2 (.in(in_1), .\dist (3'b001), .out(shifter_2_out));
  Adder adder_2 (.a(in_1), .b(8'h1), .out(adder_2_out));  // open: cin, cout
  and and_3 (and_3_out, adder_1_cout, decoder_1_out1);
  or or_2 (Overflow, and_3_out, and_2_out);
  nor nor_1 (Zero, in_1[0], in_1[1], in_1[2], in_1[3], in_1[4], in_1[5], in_1[6], in_1[7]);
  not not_2 (NotZero, nor_2_out);
  nor nor_2 (nor_2_out, in_1[0], in_1[1], in_1[2], in_1[3], in_1[4], in_1[5], in_1[6], in_1[7]);
  and and_4 (Negative, SUB_2_out_4, decoder_1_out2);
  or or_3 (or_3_out, multiplier_1_cout[0], multiplier_1_cout[1], multiplier_1_cout[2], multiplier_1_cout[3], multiplier_1_cout[4], multiplier_1_cout[5], multiplier_1_cout[6], multiplier_1_cout[7]);
  Multiplexer #(.select(4), .width(8), .enable("false")) multiplexer_1 (
    .in1(adder_1_out), .in2(SUB_2_out_3), .in3(multiplier_1_out), .in4(divider_1_out), .in5(and_1_out),
    .in6(or_1_out), .in7(xor_1_out), .in8(not_1_out), .in9(shifter_1_out), .in10(shifter_2_out),
    .in11(SUB_out_3), .in12(adder_2_out), .in13(undriven), .in14(undriven_2), .in15(undriven_3),
    .out(multiplexer_1_out), .sel(priority_encoder_1_p1));  // open: in0
  or or_4 (or_4_out[0], ADD, MUL);
  or or_5 (or_4_out[1], SUB, MUL);
  // Probe on priority_encoder_1_p1
  // Priority_Encoder #(.select(4)) priority_encoder_1: pin names not known; wires that end beside it: priority_encoder_1_p1, ADD, SUB, MUL, DIV, AND, OR, XOR, CMA, RAL, RAR, DCR, INR
  assign out_16 = or_6_out ? multiplexer_1_out : 8'bz;  // Controlled_Buffer controlled_buffer_1
  or or_6 (or_6_out, 1'b0, INR, DCR, RAR, RAL, CMA, XOR, OR, AND, DIV, MUL, SUB, ADD);

  assign Negative_2 = in_1[7];
endmodule

module TMP (
  input  Ltm,
  input  [7:0] in_2,
  input  CLK,
  input  CLR,
  input  Etm,
  output [7:0] out_6,
  output [7:0] out_7,
  output [7:0] out_8
);

  wire not_1_out;

  Register register_1 (.D(in_2), .en(Ltm), .Q(out_6), .clk(not_1_out), .clr(CLR));
  not not_1 (not_1_out, CLK);
  assign out_8 = Etm ? out_6 : 8'bz;  // Controlled_Buffer controlled_buffer_1

  assign out_7 = out_6;

  // Notes on the sheet:
  //   For ALU
endmodule

module B_Reg (
  input  Lb,
  input  [7:0] in_2,
  input  CLK,
  input  CLR,
  input  Eb,
  output [7:0] out_6
);

  wire not_1_out;
  wire [7:0] register_1_q;

  Register register_1 (.D(in_2), .en(Lb), .Q(register_1_q), .clk(not_1_out), .clr(CLR));
  not not_1 (not_1_out, CLK);
  assign out_6 = Eb ? register_1_q : 8'bz;  // Controlled_Buffer controlled_buffer_1
endmodule

module C_Reg (
  input  Lb,
  input  [7:0] in_2,
  input  CLK,
  input  CLR,
  input  Eb,
  output [7:0] out_6
);

  wire not_1_out;
  wire [7:0] register_1_q;

  Register register_1 (.D(in_2), .en(Lb), .Q(register_1_q), .clk(not_1_out), .clr(CLR));
  not not_1 (not_1_out, CLK);
  assign out_6 = Eb ? register_1_q : 8'bz;  // Controlled_Buffer controlled_buffer_1
endmodule

module Out_port_3 (
  input  [7:0] minus_Lo,
  input  CLK,
  input  in_3,
  input  CLR,
  output [7:0] out_5
);

  wire not_1_out;

  Register register_1 (.D(minus_Lo), .en(CLK), .Q(out_5), .clk(not_1_out), .clr(CLR));
  not not_1 (not_1_out, in_3);

  // Notes on the sheet:
  //   For Display
endmodule

module Out_port_4 (
  input  [7:0] in_1,
  input  Lo4,
  input  CLK,
  input  CLR,
  output Serial_Out,
  output ACKNOWLEDGE
);

  wire not_1_out;
  wire [6:1] register_1_q;

  Register register_1 (.D(in_1), .en(Lo4), .Q({ACKNOWLEDGE, register_1_q, Serial_Out}), .clk(not_1_out), .clr(CLR));
  not not_1 (not_1_out, CLK);
endmodule

module SUB_2_s (
  input  [7:0] in_1,
  input  [7:0] in_2,
  output [7:0] out_3,
  output out_4
);

  wire and_1_out, and_2_out, and_3_out, and_4_out, nor_1_out, not_1_out, not_2_out, or_1_out, or_2_out;
  wire [1:0] subtractor_1_bout;
  wire [6:0] adder_1_out, bit_extender_1_out, bit_extender_2_out, subtractor_1_out, subtractor_2_out;

  // Probe on bit_extender_1_out
  Bit_Extender #(.out_width(7)) bit_extender_1 (.in(in_1), .out(bit_extender_1_out));
  Bit_Extender #(.out_width(7)) bit_extender_2 (.in(in_2), .out(bit_extender_2_out));
  // Probe on bit_extender_2_out
  xor xor_1 (subtractor_1_bout[1], in_1[7], in_2[7]);
  Subtractor #(.width(7)) subtractor_1 (
    .a(bit_extender_1_out), .b(bit_extender_2_out), .out(subtractor_1_out), .bout(subtractor_1_bout[0]));  // open: bin
  Adder #(.width(7)) adder_1 (.a(bit_extender_1_out), .b(bit_extender_2_out), .out(adder_1_out));  // open: cin, cout
  Subtractor #(.width(7)) subtractor_2 (
    .a(bit_extender_2_out), .b(bit_extender_1_out), .out(subtractor_2_out));  // open: bin, bout
  // Probe on adder_1_out
  Multiplexer #(.select(2), .width(7), .enable("false")) multiplexer_1 (
    .in0(subtractor_1_out), .in1(subtractor_2_out), .in2(adder_1_out), .in3(adder_1_out), .out(out_3[6:0]),
    .sel(subtractor_1_bout));
  // Probe on out_3[6:0]
  nor nor_1 (nor_1_out, in_1[7], in_2[7]);
  not not_1 (not_1_out, in_2[7]);
  and and_1 (and_1_out, in_1[7], in_2[7]);
  not not_2 (not_2_out, subtractor_1_bout[0]);
  or or_1 (or_1_out, and_3_out, and_4_out, and_2_out);
  and and_2 (and_2_out, subtractor_1_bout[0], nor_1_out);
  and and_3 (and_3_out, in_1[7], not_1_out);
  and and_4 (and_4_out, and_1_out, not_2_out);
  or or_2 (or_2_out, out_3[0], out_3[1], out_3[2], out_3[3], out_3[4], out_3[5], out_3[6]);
  and and_5 (out_3[7], or_2_out, or_1_out);

  assign out_4 = out_3[7];
endmodule
